// Logisim project Ejercicio2.circ as structural Verilog
module main (
  input  Procesar,
  input  [2:0] ABC,
  input  [2:0] DEF,
  input  [2:0] GHI,
  output [2:0] out_5
);

  wire decoder_1_out0, decoder_1_out1, decoder_1_out2, decoder_1_out3, decoder_1_out4, decoder_1_out5,
       decoder_1_out6, decoder_1_out7;

  Decoder #(.select(3)) decoder_1 (
    .out0(decoder_1_out0), .out1(decoder_1_out1), .out2(decoder_1_out2), .out3(decoder_1_out3),
    .out4(decoder_1_out4), .out5(decoder_1_out5), .out6(decoder_1_out6), .out7(decoder_1_out7), .sel(ABC),
    .en(Procesar));
  Memoria_Interna memoria_interna_1 (
    .EntradaDatos(GHI), .EscribirAMemoria(decoder_1_out0), .Address(DEF), .ClearMemory(decoder_1_out4),
    .Salida(out_5));
endmodule

module Memoria_Interna (
  input  [2:0] EntradaDatos,
  input  EscribirAMemoria,
  input  [2:0] Address,
  input  ClearMemory,
  output [2:0] Salida
);

  wire decoder_1_out0, decoder_1_out1, decoder_1_out2, decoder_1_out3, decoder_1_out4, decoder_1_out5,
       decoder_1_out6, decoder_1_out7;
  wire [2:0] d_ff_1_q, d_ff_4_q, d_ff_7_q, d_ff_10_q, d_ff_13_q, d_ff_16_q, d_ff_19_q, d_ff_22_q;

  Decoder #(.select(3)) decoder_1 (
    .out0(decoder_1_out0), .out1(decoder_1_out1), .out2(decoder_1_out2), .out3(decoder_1_out3),
    .out4(decoder_1_out4), .out5(decoder_1_out5), .out6(decoder_1_out6), .out7(decoder_1_out7),
    .sel(Address), .en(EscribirAMemoria));
  Multiplexer #(.select(3), .width(3)) multiplexer_1 (
    .in0(d_ff_1_q), .in1(d_ff_4_q), .in2(d_ff_7_q), .in3(d_ff_10_q), .in4(d_ff_13_q), .in5(d_ff_16_q),
    .in6(d_ff_19_q), .in7(d_ff_22_q), .out(Salida), .sel(Address));
  D_Flip_Flop d_ff_1 (
    .D(EntradaDatos[0]), .clk(decoder_1_out0), .Q(d_ff_1_q[0]), .reset(ClearMemory));  // open: Qn, preset
  D_Flip_Flop d_ff_2 (
    .D(EntradaDatos[1]), .clk(decoder_1_out0), .Q(d_ff_1_q[1]), .reset(ClearMemory));  // open: Qn, preset
  D_Flip_Flop d_ff_3 (
    .D(EntradaDatos[2]), .clk(decoder_1_out0), .Q(d_ff_1_q[2]), .reset(ClearMemory));  // open: Qn, preset
  D_Flip_Flop d_ff_4 (
    .D(EntradaDatos[0]), .clk(decoder_1_out1), .Q(d_ff_4_q[0]), .reset(ClearMemory));  // open: Qn, preset
  D_Flip_Flop d_ff_5 (
    .D(EntradaDatos[1]), .clk(decoder_1_out1), .Q(d_ff_4_q[1]), .reset(ClearMemory));  // open: Qn, preset
  D_Flip_Flop d_ff_6 (
    .D(EntradaDatos[2]), .clk(decoder_1_out1), .Q(d_ff_4_q[2]), .reset(ClearMemory));  // open: Qn, preset
  D_Flip_Flop d_ff_7 (
    .D(EntradaDatos[0]), .clk(decoder_1_out2), .Q(d_ff_7_q[0]), .reset(ClearMemory));  // open: Qn, preset
  D_Flip_Flop d_ff_8 (
    .D(EntradaDatos[1]), .clk(decoder_1_out2), .Q(d_ff_7_q[1]), .reset(ClearMemory));  // open: Qn, preset
  D_Flip_Flop d_ff_9 (
    .D(EntradaDatos[2]), .clk(decoder_1_out2), .Q(d_ff_7_q[2]), .reset(ClearMemory));  // open: Qn, preset
  D_Flip_Flop d_ff_10 (
    .D(EntradaDatos[0]), .clk(decoder_1_out3), .Q(d_ff_10_q[0]), .reset(ClearMemory));  // open: Qn, preset
  D_Flip_Flop d_ff_11 (
    .D(EntradaDatos[1]), .clk(decoder_1_out3), .Q(d_ff_10_q[1]), .reset(ClearMemory));  // open: Qn, preset
  D_Flip_Flop d_ff_12 (
    .D(EntradaDatos[2]), .clk(decoder_1_out3), .Q(d_ff_10_q[2]), .reset(ClearMemory));  // open: Qn, preset
  D_Flip_Flop d_ff_13 (
    .D(EntradaDatos[0]), .clk(decoder_1_out4), .Q(d_ff_13_q[0]), .reset(ClearMemory));  // open: Qn, preset
  D_Flip_Flop d_ff_14 (
    .D(EntradaDatos[1]), .clk(decoder_1_out4), .Q(d_ff_13_q[1]), .reset(ClearMemory));  // open: Qn, preset
  D_Flip_Flop d_ff_15 (
    .D(EntradaDatos[2]), .clk(decoder_1_out4), .Q(d_ff_13_q[2]), .reset(ClearMemory));  // open: Qn, preset
  D_Flip_Flop d_ff_16 (
    .D(EntradaDatos[0]), .clk(decoder_1_out5), .Q(d_ff_16_q[0]), .reset(ClearMemory));  // open: Qn, preset
  D_Flip_Flop d_ff_17 (
    .D(EntradaDatos[1]), .clk(decoder_1_out5), .Q(d_ff_16_q[1]), .reset(ClearMemory));  // open: Qn, preset
  D_Flip_Flop d_ff_18 (
    .D(EntradaDatos[2]), .clk(decoder_1_out5), .Q(d_ff_16_q[2]), .reset(ClearMemory));  // open: Qn, preset
  D_Flip_Flop d_ff_19 (
    .D(EntradaDatos[0]), .clk(decoder_1_out6), .Q(d_ff_19_q[0]), .reset(ClearMemory));  // open: Qn, preset
  D_Flip_Flop d_ff_20 (
    .D(EntradaDatos[1]), .clk(decoder_1_out6), .Q(d_ff_19_q[1]), .reset(ClearMemory));  // open: Qn, preset
  D_Flip_Flop d_ff_21 (
    .D(EntradaDatos[2]), .clk(decoder_1_out6), .Q(d_ff_19_q[2]), .reset(ClearMemory));  // open: Qn, preset
  D_Flip_Flop d_ff_22 (
    .D(EntradaDatos[0]), .clk(decoder_1_out7), .Q(d_ff_22_q[0]), .reset(ClearMemory));  // open: Qn, preset
  D_Flip_Flop d_ff_23 (
    .D(EntradaDatos[1]), .clk(decoder_1_out7), .Q(d_ff_22_q[1]), .reset(ClearMemory));  // open: Qn, preset
  D_Flip_Flop d_ff_24 (
    .D(EntradaDatos[2]), .clk(decoder_1_out7), .Q(d_ff_22_q[2]), .reset(ClearMemory));  // open: Qn, preset
endmodule

module FlipFlop_TipoD (
  input  D,
  input  P,
  output out_3
);

  wire nand_1_out, nand_2_out, nand_4_out, not_1_out;

  not not_1 (not_1_out, D);
  nand nand_1 (nand_1_out, D, P);
  nand nand_2 (nand_2_out, not_1_out, P);
  nand nand_3 (out_3, nand_1_out, nand_4_out);
  nand nand_4 (nand_4_out, out_3, nand_2_out);
endmodule
